# Fritzing sketch gc20230606 (saved by Fritzing 0.9.9b)
circuit board: 9.5cm x 6cm
breadboards: 1

parts:
  PCF8574 = PCF8574 [package="DIP16 [THT]"]
  J3 = female pin header, 7 pins [form="♀ (female)"]
  P1 = Pushbutton [package="[THT]"]
  P2 = Pushbutton [package="[THT]"]
  P3 = Pushbutton [package="[THT]"]
  P0 = Pushbutton [package="[THT]"]
  P5 = Pushbutton [package="[THT]"]
  P4 = Pushbutton [package="[THT]"]
  10k = Resistor [tolerance=±5% resistance=220 power=0.25 package=THT]
  10k_2 = Resistor [tolerance=±5% resistance=220 power=0.25 package=THT]
  10k_3 = Resistor [tolerance=±5% resistance=220 power=0.25 package=THT]
  10k_4 = Resistor [tolerance=±5% resistance=220 power=0.25 package=THT]
  10k_5 = Resistor [tolerance=±5% resistance=220 power=0.25 package=THT]
  WeMos_D1_Mini = WeMos D1 Mini
  10k_6 = Resistor [tolerance=±5% power=0.25 resistance=220 package=THT]

nets:
  N1: PCF8574.A0, PCF8574.A1, PCF8574.A2, PCF8574.GND, J3.pin1, P1.Pin_1, P1.Pin_2, P2.Pin_1, P2.Pin_2, P3.Pin_1, P3.Pin_2, P0.Pin_1, P0.Pin_2, P5.Pin_1, P5.Pin_2, P4.Pin_1, P4.Pin_2, WeMos_D1_Mini.G
  N2: PCF8574.P0, P0.Pin_3, P0.Pin_4, 10k_2.Pin_1
  N3: PCF8574.P1, P1.Pin_3, P1.Pin_4, 10k_5.Pin_0
  N4: PCF8574.P2, P2.Pin_3, P2.Pin_4, 10k_4.Pin_1
  N5: PCF8574.P3, P3.Pin_3, P3.Pin_4, 10k_3.Pin_0
  N6: PCF8574.P4, P4.Pin_3, P4.Pin_4, 10k_6.Pin_0
  N7: PCF8574.P5, P5.Pin_3, P5.Pin_4, 10k.Pin_1
  N8: PCF8574.SCL, WeMos_D1_Mini.D1
  N9: PCF8574.SDA, WeMos_D1_Mini.D2
  VCC: PCF8574.VCC, J3.pin2, 10k.Pin_0, 10k_2.Pin_0, 10k_3.Pin_1, 10k_4.Pin_0, 10k_5.Pin_1, WeMos_D1_Mini.3V3, 10k_6.Pin_1
  N10: J3.pin3, WeMos_D1_Mini.D5
  N11: J3.pin4, WeMos_D1_Mini.D7
  N12: J3.pin5, WeMos_D1_Mini.D6
  N13: J3.pin6, WeMos_D1_Mini.D8
  N14: J3.pin7, WeMos_D1_Mini.D0

notes:
  Model: GC20230606
  - + C DA RS DC B
  ST7789
  SDA
  SCL
  P4
  P5
  P0
  P1
  P2
  P3
